// Logisim project TP01 3ra parte.circ as structural Verilog: 1 circuit, main circuit Enunciado00
module Enunciado00 (
  input  D
);

  wire and_1_out, and_2_out, CK_out, or_1_out;

  Clock CK (.out(CK_out));
  and and_1 (and_1_out, D, CK_out);
  and and_2 (and_2_out, ~CK_out, or_1_out);  // AND_Gate
  D_Flip_Flop d_ff_1 ();  // open: clk, D, Q, Qn, preset, en, reset
  or or_1 (or_1_out, and_1_out, and_2_out);
endmodule
