// Logisim project TP01 4ta parte.circ as structural Verilog: 2 circuits, main circuit Memoria SRAM
module Memoria_SRAM (
  input  [3:0] in_1,
  input  Lectura_Escritura,
  input  [1:0] in_3
);

  wire and_1_out, and_2_out, and_3_out, and_4_out, decoder_1_out0, decoder_1_out1, decoder_1_out2,
       decoder_1_out3, not_1_out;

  not not_1 (not_1_out, Lectura_Escritura);
  Decoder #(.select(2), .disabled(0), .enable("false")) decoder_1 (
    .out0(decoder_1_out0), .out1(decoder_1_out1), .out2(decoder_1_out2), .out3(decoder_1_out3), .sel(in_3));
  and and_1 (and_1_out, not_1_out, decoder_1_out0);
  and and_2 (and_2_out, not_1_out, decoder_1_out1);
  and and_3 (and_3_out, not_1_out, decoder_1_out2);
  and and_4 (and_4_out, not_1_out, decoder_1_out3);
  D_Flip_Flop d_ff_1 (.clk(and_1_out), .D(in_1[3]));  // open: Q, Qn, preset, en, reset
  D_Flip_Flop d_ff_2 (.clk(and_2_out), .D(in_1[3]));  // open: Q, Qn, preset, en, reset
  D_Flip_Flop d_ff_3 (.clk(and_3_out), .D(in_1[3]));  // open: Q, Qn, preset, en, reset
  D_Flip_Flop d_ff_4 (.clk(and_4_out), .D(in_1[3]));  // open: Q, Qn, preset, en, reset
  D_Flip_Flop d_ff_5 (.clk(and_1_out), .D(in_1[2]));  // open: Q, Qn, preset, en, reset
  D_Flip_Flop d_ff_6 (.clk(and_2_out), .D(in_1[2]));  // open: Q, Qn, preset, en, reset
  D_Flip_Flop d_ff_7 (.clk(and_3_out), .D(in_1[2]));  // open: Q, Qn, preset, en, reset
  D_Flip_Flop d_ff_8 (.clk(and_4_out), .D(in_1[2]));  // open: Q, Qn, preset, en, reset
  D_Flip_Flop d_ff_9 (.clk(and_1_out), .D(in_1[1]));  // open: Q, Qn, preset, en, reset
  D_Flip_Flop d_ff_10 (.clk(and_2_out), .D(in_1[1]));  // open: Q, Qn, preset, en, reset
  D_Flip_Flop d_ff_11 (.clk(and_3_out), .D(in_1[1]));  // open: Q, Qn, preset, en, reset
  D_Flip_Flop d_ff_12 (.clk(and_4_out), .D(in_1[1]));  // open: Q, Qn, preset, en, reset
  D_Flip_Flop d_ff_13 (.clk(and_1_out), .D(in_1[0]));  // open: Q, Qn, preset, en, reset
  D_Flip_Flop d_ff_14 (.clk(and_2_out), .D(in_1[0]));  // open: Q, Qn, preset, en, reset
  D_Flip_Flop d_ff_15 (.clk(and_3_out), .D(in_1[0]));  // open: Q, Qn, preset, en, reset
  D_Flip_Flop d_ff_16 (.clk(and_4_out), .D(in_1[0]));  // open: Q, Qn, preset, en, reset
endmodule

module FFMaestroEsclavo (
  input  D
);

  wire and_1_out, and_2_out, and_3_out, and_4_out, CK_out, not_1_out, or_1_out, or_2_out;

  Clock CK (.out(CK_out));
  not not_1 (not_1_out, CK_out);
  and and_1 (and_1_out, D, not_1_out);
  and and_2 (and_2_out, ~not_1_out, or_1_out);  // AND_Gate
  or or_1 (or_1_out, and_1_out, and_2_out);
  and and_3 (and_3_out, or_1_out, CK_out);
  and and_4 (and_4_out, ~CK_out, or_2_out);  // AND_Gate
  or or_2 (or_2_out, and_3_out, and_4_out);
endmodule
