// Logisim project TP1 4ta parte.circ as structural Verilog: 6 circuits, main circuit Memoria SRAM
module Memoria_SRAM (
  input  [3:0] in_1,
  input  Lec_1__Esc_0,
  input  [1:0] in_3
);

  wire and_1_out, and_2_out, and_3_out, and_4_out, and_5_out, and_6_out, and_7_out, and_8_out, and_9_out,
       and_10_out, and_11_out, and_12_out, and_13_out, and_14_out, and_15_out, and_16_out, and_17_out,
       and_18_out, and_19_out, and_20_out, controlled_buffer_1_out, controlled_buffer_2_out,
       controlled_buffer_3_out, controlled_buffer_4_out, d_ff_1_q, d_ff_2_q, d_ff_3_q, d_ff_4_q, d_ff_5_q,
       d_ff_6_q, d_ff_7_q, d_ff_8_q, d_ff_9_q, d_ff_10_q, d_ff_11_q, d_ff_12_q, d_ff_13_q, d_ff_14_q,
       d_ff_15_q, d_ff_16_q, decoder_1_out0, decoder_1_out1, decoder_1_out2, decoder_1_out3, not_1_out,
       or_1_out, or_2_out, or_3_out, or_4_out;

  // Probe on controlled_buffer_1_out
  // Probe on controlled_buffer_2_out
  // Probe on controlled_buffer_3_out
  // Probe on controlled_buffer_4_out
  Decoder #(.select(2), .disabled(0), .enable("false")) decoder_1 (
    .out0(decoder_1_out0), .out1(decoder_1_out1), .out2(decoder_1_out2), .out3(decoder_1_out3), .sel(in_3));
  not not_1 (not_1_out, Lec_1__Esc_0);
  and and_1 (and_1_out, not_1_out, decoder_1_out0);
  and and_2 (and_2_out, not_1_out, decoder_1_out1);
  and and_3 (and_3_out, not_1_out, decoder_1_out2);
  and and_4 (and_4_out, not_1_out, decoder_1_out3);
  D_Flip_Flop d_ff_1 (.clk(and_1_out), .D(in_1[3]), .Q(d_ff_1_q));  // open: Qn, preset, en, reset
  and and_5 (and_5_out, decoder_1_out0, d_ff_1_q);
  D_Flip_Flop d_ff_2 (.clk(and_2_out), .D(in_1[3]), .Q(d_ff_2_q));  // open: Qn, preset, en, reset
  and and_6 (and_6_out, decoder_1_out1, d_ff_2_q);
  D_Flip_Flop d_ff_3 (.clk(and_3_out), .D(in_1[3]), .Q(d_ff_3_q));  // open: Qn, preset, en, reset
  and and_7 (and_7_out, decoder_1_out2, d_ff_3_q);
  D_Flip_Flop d_ff_4 (.clk(and_4_out), .D(in_1[3]), .Q(d_ff_4_q));  // open: Qn, preset, en, reset
  and and_8 (and_8_out, decoder_1_out3, d_ff_4_q);
  or or_1 (or_1_out, and_8_out, and_7_out, and_6_out, and_5_out);
  D_Flip_Flop d_ff_5 (.clk(and_1_out), .D(in_1[2]), .Q(d_ff_5_q));  // open: Qn, preset, en, reset
  and and_9 (and_9_out, decoder_1_out0, d_ff_5_q);
  D_Flip_Flop d_ff_6 (.clk(and_2_out), .D(in_1[2]), .Q(d_ff_6_q));  // open: Qn, preset, en, reset
  and and_10 (and_10_out, decoder_1_out1, d_ff_6_q);
  D_Flip_Flop d_ff_7 (.clk(and_3_out), .D(in_1[2]), .Q(d_ff_7_q));  // open: Qn, preset, en, reset
  and and_11 (and_11_out, decoder_1_out2, d_ff_7_q);
  D_Flip_Flop d_ff_8 (.clk(and_4_out), .D(in_1[2]), .Q(d_ff_8_q));  // open: Qn, preset, en, reset
  and and_12 (and_12_out, decoder_1_out3, d_ff_8_q);
  or or_2 (or_2_out, and_12_out, and_11_out, and_10_out, and_9_out);
  D_Flip_Flop d_ff_9 (.clk(and_1_out), .D(in_1[1]), .Q(d_ff_9_q));  // open: Qn, preset, en, reset
  and and_13 (and_13_out, decoder_1_out0, d_ff_9_q);
  D_Flip_Flop d_ff_10 (.clk(and_2_out), .D(in_1[1]), .Q(d_ff_10_q));  // open: Qn, preset, en, reset
  and and_14 (and_14_out, decoder_1_out1, d_ff_10_q);
  D_Flip_Flop d_ff_11 (.clk(and_3_out), .D(in_1[1]), .Q(d_ff_11_q));  // open: Qn, preset, en, reset
  and and_15 (and_15_out, decoder_1_out2, d_ff_11_q);
  D_Flip_Flop d_ff_12 (.clk(and_4_out), .D(in_1[1]), .Q(d_ff_12_q));  // open: Qn, preset, en, reset
  and and_16 (and_16_out, decoder_1_out3, d_ff_12_q);
  or or_3 (or_3_out, and_16_out, and_15_out, and_14_out, and_13_out);
  assign controlled_buffer_1_out = Lec_1__Esc_0 ? or_1_out : 1'bz;  // Controlled_Buffer controlled_buffer_1
  assign controlled_buffer_2_out = Lec_1__Esc_0 ? or_2_out : 1'bz;  // Controlled_Buffer controlled_buffer_2
  assign controlled_buffer_3_out = Lec_1__Esc_0 ? or_3_out : 1'bz;  // Controlled_Buffer controlled_buffer_3
  assign controlled_buffer_4_out = Lec_1__Esc_0 ? or_4_out : 1'bz;  // Controlled_Buffer controlled_buffer_4
  D_Flip_Flop d_ff_13 (.clk(and_1_out), .D(in_1[0]), .Q(d_ff_13_q));  // open: Qn, preset, en, reset
  and and_17 (and_17_out, decoder_1_out0, d_ff_13_q);
  D_Flip_Flop d_ff_14 (.clk(and_2_out), .D(in_1[0]), .Q(d_ff_14_q));  // open: Qn, preset, en, reset
  and and_18 (and_18_out, decoder_1_out1, d_ff_14_q);
  D_Flip_Flop d_ff_15 (.clk(and_3_out), .D(in_1[0]), .Q(d_ff_15_q));  // open: Qn, preset, en, reset
  and and_19 (and_19_out, decoder_1_out2, d_ff_15_q);
  D_Flip_Flop d_ff_16 (.clk(and_4_out), .D(in_1[0]), .Q(d_ff_16_q));  // open: Qn, preset, en, reset
  and and_20 (and_20_out, decoder_1_out3, d_ff_16_q);
  or or_4 (or_4_out, and_20_out, and_19_out, and_18_out, and_17_out);
endmodule

module FFMaestroEsclavo (
  input  D,
  input  in_2
);

  wire and_1_out, and_2_out, and_3_out, and_4_out, CK_out, clock_1_out, d_ff_1_q, d_ff_2_q, not_1_out,
       not_2_out, or_1_out, or_2_out;

  Clock CK (.out(CK_out));
  not not_1 (not_1_out, clock_1_out);
  Clock clock_1 (.out(clock_1_out));
  not not_2 (not_2_out, CK_out);
  and and_1 (and_1_out, D, not_2_out);
  and and_2 (and_2_out, ~not_2_out, or_1_out);  // AND_Gate
  D_Flip_Flop d_ff_1 (.clk(not_1_out), .D(in_2), .Q(d_ff_1_q));  // open: Qn, preset, en, reset
  or or_1 (or_1_out, and_1_out, and_2_out);
  D_Flip_Flop d_ff_2 (.clk(clock_1_out), .D(d_ff_1_q), .Q(d_ff_2_q));  // open: Qn, preset, en, reset
  // Probe on d_ff_2_q
  and and_3 (and_3_out, or_1_out, CK_out);
  and and_4 (and_4_out, ~CK_out, or_2_out);  // AND_Gate
  or or_2 (or_2_out, and_3_out, and_4_out);
endmodule

module DataBus (
  input  [3:0] in_1,
  input  [3:0] in_2,
  input  in_3,
  input  in_4,
  input  in_5,
  input  in_6,
  input  in_7,
  input  in_8,
  input  in_9,
  output [3:0] out_10,
  output out_11,
  output [1:0] out_12,
  output [3:0] out_13
);

  wire [3:0] undriven;

  Shift_Register #(.width(4), .length(4)) shift_register_1 (
    .in(undriven), .out(out_13));  // open: shift, clk, load, clr, d0, q0, d1, q1, d2, q2, d3, q3
  Register register_1 ();  // open: D, en, Q, clk, clr
  BitSelector #(.width(4), .group(4)) bitselector_1 (.out(in_2));  // open: in, sel
  Register #(.width(4)) register_2 (.D(undriven));  // open: en, Q, clk, clr
  Controlled_Buffer controlled_buffer_1 ();  // open: in, out, en
  RAM #(.addrWidth(4), .dataWidth(4)) ram_1 (.addr(in_1), .data(out_10), .ld(in_3));  // open: sel, clk, clr
  Priority_Encoder #(.select(2)) priority_encoder_1 (
    .in0(in_4), .in1(in_6), .in2(in_7), .in3(in_8), .out(out_12), .gs(in_5), .en_out(out_11), .en_in(in_9));
  Controlled_Inverter controlled_inverter_1 ();  // open: in, out, en
endmodule

module RegistrosDLatch (
);

  Clock clock_1 ();  // open: out
  D_Flip_Flop d_ff_1 ();  // open: clk, D, Q, Qn, preset, en, reset
  D_Flip_Flop d_ff_2 ();  // open: clk, D, Q, Qn, preset, en, reset
endmodule

module Enunciado14 (
  input  d0_0,
  input  d1_0,
  input  c_0,
  input  q0_1,
  input  q1_1
);

  wire d_ff_1_p2, d_ff_1_p3, d_ff_4_q, d_ff_4_qn, not_1_out;

  not not_1 (not_1_out, c_0);
  // D_Flip_Flop d_ff_1: pin names not known; wires that end beside it: d0_0, d_ff_1_p2, d_ff_1_p3, d1_0
  D_Flip_Flop d_ff_2 (.clk(not_1_out), .Q(d_ff_1_p2), .Qn(d_ff_1_p3));  // open: D, preset, en, reset
  D_Flip_Flop d_ff_3 (.clk(d_ff_4_q), .D(d_ff_4_qn), .en(q1_1));  // open: Q, Qn, preset, reset
  D_Flip_Flop d_ff_4 (.D(c_0), .Q(d_ff_4_q), .Qn(d_ff_4_qn), .en(q0_1));  // open: clk, preset, reset

  // Notes on the sheet:
  //   c=1
  //   c=0
  //   maestro
  //   esclavo
endmodule

module RegistrosME (
  input  in_1,
  input  in_2,
  input  [3:0] in_3
);

  wire clock_1_out, d_ff_1_q, d_ff_2_q, d_ff_3_q, d_ff_4_q, d_ff_5_q, d_ff_6_q, d_ff_7_q, d_ff_8_q, d_ff_9_q,
       d_ff_10_q, not_1_out, not_2_out;

  Clock clock_1 (.out(clock_1_out));
  not not_1 (not_1_out, clock_1_out);
  not not_2 (not_2_out, in_2);
  D_Flip_Flop d_ff_1 (.clk(not_1_out), .D(in_1), .Q(d_ff_1_q));  // open: Qn, preset, en, reset
  D_Flip_Flop d_ff_2 (.clk(not_2_out), .D(in_3[3]), .Q(d_ff_2_q));  // open: Qn, preset, en, reset
  D_Flip_Flop d_ff_3 (.clk(in_2), .D(d_ff_2_q), .Q(d_ff_3_q));  // open: Qn, preset, en, reset
  D_Flip_Flop d_ff_4 (.clk(clock_1_out), .D(d_ff_1_q), .Q(d_ff_4_q));  // open: Qn, preset, en, reset
  // Probe on d_ff_3_q
  // Probe on d_ff_4_q
  D_Flip_Flop d_ff_5 (.clk(not_2_out), .D(in_3[2]), .Q(d_ff_5_q));  // open: Qn, preset, en, reset
  D_Flip_Flop d_ff_6 (.clk(in_2), .D(d_ff_5_q), .Q(d_ff_6_q));  // open: Qn, preset, en, reset
  // Probe on d_ff_6_q
  D_Flip_Flop d_ff_7 (.clk(not_2_out), .D(in_3[1]), .Q(d_ff_7_q));  // open: Qn, preset, en, reset
  D_Flip_Flop d_ff_8 (.clk(in_2), .D(d_ff_7_q), .Q(d_ff_8_q));  // open: Qn, preset, en, reset
  // Probe on d_ff_8_q
  D_Flip_Flop d_ff_9 (.clk(not_2_out), .D(in_3[0]), .Q(d_ff_9_q));  // open: Qn, preset, en, reset
  D_Flip_Flop d_ff_10 (.clk(in_2), .D(d_ff_9_q), .Q(d_ff_10_q));  // open: Qn, preset, en, reset
  // Probe on d_ff_10_q
endmodule
