// Logisim project Unidad 1 Clase 1 TP1 Punto 1.circ as structural Verilog
module P01 (
  input  A,
  input  B,
  input  C,
  output Z
);

  and and_1 (Z, ~A, B, C);  // AND_Gate
endmodule

module P02 (
  input  A,
  input  B,
  input  C,
  output Z0,
  output Z1
);

  and and_1 (Z0, ~A, B, ~C);  // AND_Gate
  and and_2 (Z1, ~A, B, C);  // AND_Gate
endmodule

module P03 (
  input  A,
  input  B,
  input  C,
  output Z0,
  output Z1,
  output Z2,
  output Z3,
  output Z4,
  output Z5,
  output Z6,
  output Z7
);

  and and_1 (Z0, ~A, ~B, ~C);  // AND_Gate
  and and_2 (Z1, ~A, ~B, C);  // AND_Gate
  and and_3 (Z2, ~A, B, ~C);  // AND_Gate
  and and_4 (Z3, ~A, B, C);  // AND_Gate
  and and_5 (Z4, A, ~B, ~C);  // AND_Gate
  and and_6 (Z5, A, ~B, C);  // AND_Gate
  and and_7 (Z6, A, B, ~C);  // AND_Gate
  and and_8 (Z7, A, B, C);
endmodule

module P04 (
  input  A,
  input  B,
  input  C,
  output Z
);

  wire and_1_out, and_2_out;

  and and_1 (and_1_out, ~A, B, ~C);  // AND_Gate
  and and_2 (and_2_out, ~A, B, C);  // AND_Gate
  or or_1 (Z, and_1_out, and_2_out);
endmodule

module P05 (
  input  A,
  input  B,
  output Z
);

  wire and_1_out, and_2_out;

  and and_1 (and_1_out, ~A, B);  // AND_Gate
  and and_2 (and_2_out, A, ~B);  // AND_Gate
  or or_1 (Z, and_1_out, and_2_out);
endmodule
