// Logisim project Unidad 1 TP1 2da Parte.circ as structural Verilog: 4 circuits, main circuit P06
module P06 (
  input  A0,
  input  A1,
  input  B0,
  input  B1,
  output Z0,
  output Z1,
  output Z2,
  output Z3
);

  wire and_2_out, and_3_out, and_4_out, and_5_out, and_6_out, and_7_out, and_8_out, and_9_out;

  and and_1 (Z0, A0, A1, B0, B1);
  and and_2 (and_2_out, A0, ~A1, B0, ~B1);  // AND_Gate
  and and_3 (and_3_out, A0, ~A1, B0, B1);  // AND_Gate
  and and_4 (and_4_out, A0, A1, B0, ~B1);  // AND_Gate
  and and_5 (and_5_out, ~A0, A1, B0, ~B1);  // AND_Gate
  and and_6 (and_6_out, A0, ~A1, ~B0, B1);  // AND_Gate
  and and_7 (and_7_out, A0, A1, ~B0, B1);  // AND_Gate
  and and_8 (and_8_out, ~A0, A1, B0, B1);  // AND_Gate
  and and_9 (and_9_out, ~A0, A1, ~B0, B1);  // AND_Gate
  or or_1 (Z1, and_2_out, and_3_out, and_4_out);
  or or_2 (Z2, and_4_out, and_3_out, and_5_out, and_6_out, and_7_out, and_8_out);
  or or_3 (Z3, Z0, and_7_out, and_8_out, and_9_out);
endmodule

module P07 (
  input  LC,
  input  [3:0] A,
  input  [3:0] B,
  output Zero,
  output [3:0] S,
  output Sign,
  output Carry,
  output Overflow
);

  wire adder_1_cout, adder_2_cout, adder_3_cout, adder_4_cout, and_1_out, and_2_out, xor_1_out, xor_2_out,
       xor_3_out, xor_4_out;

  xor xor_1 (xor_1_out, LC, B[0]);
  xor xor_2 (xor_2_out, LC, B[1]);
  xor xor_3 (xor_3_out, LC, B[2]);
  xor xor_4 (xor_4_out, LC, B[3]);
  Adder #(.width(1)) adder_1 (.a(A[0]), .b(xor_1_out), .out(S[0]), .cin(LC), .cout(adder_1_cout));
  Adder #(.width(1)) adder_2 (.a(A[1]), .b(xor_2_out), .out(S[1]), .cin(adder_1_cout), .cout(adder_2_cout));
  Adder #(.width(1)) adder_3 (.a(A[2]), .b(xor_3_out), .out(S[2]), .cin(adder_2_cout), .cout(adder_3_cout));
  Adder #(.width(1)) adder_4 (.a(A[3]), .b(xor_4_out), .out(S[3]), .cin(adder_3_cout), .cout(adder_4_cout));
  xor xor_5 (Carry, adder_4_cout, LC);
  and and_1 (and_1_out, S[3], ~A[3], ~xor_4_out);  // AND_Gate
  and and_2 (and_2_out, ~S[3], A[3], xor_4_out);  // AND_Gate
  and and_3 (Zero, ~S[0], ~S[1], ~S[2], ~S[3]);  // AND_Gate
  or or_1 (Overflow, and_1_out, and_2_out);

  assign Sign = S[3];
endmodule

module P08 (
  input  LC,
  input  A,
  input  B,
  output S,
  output Carry
);

  wire adder_1_cout, xor_1_out;

  xor xor_1 (xor_1_out, LC, B);
  Adder #(.width(1)) adder_1 (.a(A), .b(xor_1_out), .out(S), .cin(LC), .cout(adder_1_cout));
  xor xor_2 (Carry, adder_1_cout, LC);
endmodule

module P09 (
  input  LC,
  input  [3:0] A,
  input  [3:0] B,
  output [3:0] S,
  output Overflow
);

  wire adder_1_cout, adder_2_cout, adder_3_cout, and_1_out, and_2_out, xor_1_out, xor_2_out, xor_3_out,
       xor_4_out;

  xor xor_1 (xor_1_out, LC, B[0]);
  xor xor_2 (xor_2_out, LC, B[1]);
  xor xor_3 (xor_3_out, LC, B[2]);
  xor xor_4 (xor_4_out, LC, B[3]);
  Adder #(.width(1)) adder_1 (.a(A[0]), .b(xor_1_out), .out(S[0]), .cin(LC), .cout(adder_1_cout));
  Adder #(.width(1)) adder_2 (.a(A[1]), .b(xor_2_out), .out(S[1]), .cin(adder_1_cout), .cout(adder_2_cout));
  Adder #(.width(1)) adder_3 (.a(A[2]), .b(xor_3_out), .out(S[2]), .cin(adder_2_cout), .cout(adder_3_cout));
  Adder #(.width(1)) adder_4 (.a(A[3]), .b(xor_4_out), .out(S[3]), .cin(adder_3_cout));  // open: cout
  and and_1 (and_1_out, S[3], ~A[3], ~xor_4_out);  // AND_Gate
  and and_2 (and_2_out, ~S[3], A[3], xor_4_out);  // AND_Gate
  or or_1 (Overflow, and_1_out, and_2_out);
endmodule
